# Fritzing sketch CIRCUIT (saved by Fritzing 0.9.3b)

parts:
  Part1 = Arduino Uno (Rev3)
  Mod1 = zmpt101b
  Part2 = Current Sensor 5A
  Part3 = OLED Monochrome 128x64 0.96 inch [part_number=326]  # not connected
  sdCard1 = my_sdCard

nets:
  N1: Part1.A0, Mod1.OUT
  N2: Part1.A1, Part2.2, Part2.OUT
  N3: Part1.D11_PWM/MOSI, sdCard1.MOSI
  N4: Part1.D12/MISO, sdCard1.MISO
  N5: Part1.D13/SCK, sdCard1.SCK
  N6: Part1.D4, sdCard1.CS
  5V: Part1.5V, sdCard1.VCC
  GND: Part1.GND, Part2.GND

custom parts:
  zmpt101b: Single phase ac active output voltate transformer module.
  OLED Monochrome 128x64 0.96 inch: These displays are small, only about 1" diameter, but very readable due to the high contrast of an OLED display. This display is made of 128x64 individual white OLED pixels, each one is turned on or off by the controller chip. Because the display makes its own light, no backlight is required. This reduces the power required to run the OLED and is why the display has such high contrast; we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
  my_sdCard: micro sdCard Adapter with 90º pin header. Use a filtering Capacitor between CS and GND if needed. PCB View Pinouts are Reversed for laying parallel on PCB using a 90º pin header.
