# Fritzing sketch spelva-schematic (saved by Fritzing 0.9.3b)

parts:
  Part1 = Arduino Leonardo (Rev3b)
  Part2 = LCD1602-I2C
  U1 = LIPO-2000mAh [package=lipo-2000]
  A1 = Micro SD card reader
  ACS712_Current_Sensor1 = ACS712 Current Sensor
  Mod1 = zmpt101b
  Tiny_RTC1 = Tiny RTC

nets:
  N1: Part1.D4/A6, A1.Pin_2
  N2: Part1.3V3, A1.Pin_1
  VCC: Part1.5V, Part2.VCC, ACS712_Current_Sensor1.VCC, Mod1.VCC, Tiny_RTC1.VCC
  GND: Part1.GND, Part2.GND, U1.-, A1.Pin_6, ACS712_Current_Sensor1.GND, Mod1.GND, Tiny_RTC1.GND
  N3: Part1.VIN, U1.+
  N4: Part1.A0, Mod1.OUT
  N5: Part1.A1, ACS712_Current_Sensor1.OUT
  N6: Part1.A4, Part2.SDA
  N7: Part1.A5, Part2.SCL
  N8: Part1.D11_PWM, A1.Pin_3
  N9: Part1.D12/A11, A1.Pin_5
  N10: Part1.D13_PWM, A1.Pin_4

custom parts:
  LCD1602-I2C: A standard character display, usually with 2x16 characters. Comes in many colors with LCM1602 IIC attached.
  Micro SD card reader: Micro SD card reader.
  ACS712 Current Sensor: A breakout board for the Allegro ACS712 is a Hall Effect-based linear current sensor. The module operates at 5V.
  zmpt101b: Single phase ac active output voltate transformer module.
  Tiny RTC: Tiny RTC I2C module DS1370Z RTC and AT24C32 EEPROM
